# Fritzing sketch breadboard (saved by Fritzing 0.9.4)
breadboards: 1

parts:
  Part1 = Arduino Uno (Rev3) - ICSP
  Part2 = Bluetooth HC-05 Macho
  LCD1 = LCD screen
  U1 = POT_SWITCH [package=pot_pth]
  R1 = Resistor [tolerance=±5% resistance=220 package="2512 [SMD]"]

nets:
  N1: Part1.D12/MISO, LCD1.R/W
  N2: Part1.D13/SCK, LCD1.RS
  N3: Part1.D0/RX, Part2.TXD
  N4: Part1.D1/TX, Part2.RXD
  N5: Part1.D2, LCD1.DB7
  N6: Part1.D3_PWM, LCD1.DB6
  N7: Part1.D4, LCD1.DB5
  N8: Part1.D5_PWM, LCD1.DB4
  3V3: Part1.3V3, Part2.VCC
  5V: Part1.5V, LCD1.VDD, U1.G$1_A, R1.Pin_1
  GND: Part1.GND, Part2.GND, LCD1.VSS, LCD1.LED-, U1.G$1_E
  N9: LCD1.V0, U1.G$2_1
  N10: LCD1.LED+, R1.Pin_0
  N11: U1.G$2_2, U1.G$1_S
